# Fritzing sketch BMP180 (saved by Fritzing 0.9.1b)
breadboards: 1

parts:
  Raspberry_Pi1 = Raspberry Pi B+
  Part1 = Barometric Pressure Sensor - BMP180 Breakout

nets:
  3V3: Raspberry_Pi1.3v3, Part1.VCC
  N1: Raspberry_Pi1.GPIO2, Part1.SDA
  N2: Raspberry_Pi1.GPIO3, Part1.SCL
  GND: Raspberry_Pi1.GND, Part1.GND

custom parts:
  Barometric Pressure Sensor - BMP180 Breakout: Description: This is a simple breakout board for the BMP180 high-precision, low-power barometric pressure sensor. The BMP180 offers a measuring range of 300 to 1100 hPa with an absolute accuracy of down to 0.03 hPa. It's based on piezo-resistive technology for EMC robustness, high accuracy and linearity as well as long term stability. This sensor supports a voltage supply between 1.8 and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
